# Fritzing sketch 210207_Tempsensor (saved by Fritzing 0.9.4)

parts:
  RHT1 = Humidity and Temperature Sensor RHT03
  U3 = NodeMCU V3.0
  U4 = LIPO-110mAh [package=lipo-110]

nets:
  VCC: RHT1.Vcc, U3.3V3
  N1: RHT1.Data-signal, U3.D0
  N2: RHT1.GND_2, U3.GND, U4.-
  N3: U3.Vin, U4.+

custom parts:
  NodeMCU V3.0: ESP8266 based NodeMCU
